// Logisim project decode.circ as structural Verilog
module decode (
  input  [23:0] instru,
  input  We
);

  wire [7:0] data_path_1_s;
  wire [23:0] registry_24bits_1_s;

  registry_24bits registry_24bits_1 (.instru(instru), .We(We), .S(registry_24bits_1_s));
  decode_instru decode_instru_1 (.instru(registry_24bits_1_s));  // open: slctOp, slctRegA, slctRegB, slctRegWrite
  data_path data_path_1 (
    .C(data_path_1_s), .S(data_path_1_s));  // open: slctB, slctA, slctOP, slctC, sA, out_8, S7_1bit
endmodule

module decode_instru (
  input  [23:0] instru,
  output [3:0] slctOp,
  output [3:0] slctRegA,
  output [3:0] slctRegB,
  output [3:0] slctRegWrite
);

  type_op_to_slctOp type_op_to_slctop_1 (.typee(instru[23:20]), .operation(instru[19:16]), .slcOp(slctOp));

  assign slctRegA = instru[15:12];
  assign slctRegB = instru[11:8];
  assign slctRegWrite = instru[3:0];
endmodule

module type_op_to_slctOp (
  input  [3:0] typee,
  input  [3:0] operation,
  output [3:0] slcOp
);

  wire and_1_out, and_2_out, and_3_out, and_4_out, and_5_out, and_6_out, and_7_out, and_8_out, not_2_out,
       not_3_out, not_4_out;

  not not_1 (slcOp[3], typee[0]);
  not not_2 (not_2_out, operation[3]);
  not not_3 (not_3_out, operation[1]);
  not not_4 (not_4_out, operation[0]);
  and and_1 (and_1_out, typee[0], not_2_out);
  and and_2 (and_2_out, slcOp[3], operation[3]);
  and and_3 (and_3_out, slcOp[3], not_2_out, not_3_out);
  and and_4 (and_4_out, operation[2], not_3_out);
  and and_5 (and_5_out, typee[0], operation[1]);
  and and_6 (and_6_out, typee[0], operation[0]);
  and and_7 (and_7_out, not_2_out, operation[2]);
  and and_8 (and_8_out, slcOp[3], not_4_out);
  or or_1 (slcOp[2], and_1_out, and_2_out);
  or or_2 (slcOp[1], and_3_out, and_4_out, and_5_out);
  or or_3 (slcOp[0], and_6_out, and_7_out, and_8_out);
endmodule
